# Fritzing sketch LED  (saved by Fritzing 1.0.8)
breadboards: 1

parts:
  LED1 = LED - 3mm [color="Green (555nm)" current=0.030A package="3 mm [THT]"]
  R2 = Resistor [tolerance=±5% resistance=1 package="1206 [SMD]"]
  Part1 = Arduino Uno (Rev3) - ICSP
  R3 = Resistor [tolerance=±5% resistance=330 package="1206 [SMD]"]
  LED2 = LED - 3mm [color="Red (633nm)" current=0.030A package="3 mm [THT]"]
  S2 = Pushbutton [package="[THT]"]

nets:
  N1: LED1.cathode, R2.Pin_0, R2.Pin_1, S2.Pin_1, S2.Pin_2
  N2: LED1.anode, Part1.GND, R3.Pin_0, R3.Pin_1, LED2.cathode
  N3: Part1.5V, LED2.anode
  N4: S2.Pin_3, S2.Pin_4
